# Fritzing sketch Circuit (saved by Fritzing 0.9.3b)
breadboards: 2

parts:
  U1 = ESP32-38PinWide [part_number=ESP32-38PinWide]
  LED1 = LED - 5mm [color="Red (633nm)" package="5 mm [THT]"]
  LED2 = LED - 5mm [color="Green (555nm)" package="5 mm [THT]"]
  R2 = Resistor [tolerance=±5% resistance=220 package="2512 [SMD]"]
  R3 = Resistor [tolerance=±5% resistance=220 package="2512 [SMD]"]
  S1 = Pushbutton [package="[SMD]"]
  AM1 = AM2320 Humidity and Temperature Sensor [part_number="Adafruit #3721"]
  R5 = Resistor [tolerance=±5% resistance=2.2k package="2512 [SMD]"]
  R6 = Resistor [tolerance=±5% resistance=2.2k package="2512 [SMD]"]
  J2 = Dagu DGServo 9g header (male) [package=THT]
  Part1 = Adafruit TSL2561 [part_number="Adafruit #439"]

nets:
  N1: U1.GPIO21, AM1.SDA, R6.Pin_0, Part1.SDA
  N2: U1.GPIO22, AM1.SCL, R5.Pin_0, Part1.SCL
  GND: LED1.cathode, LED2.cathode, AM1.GND, J2.gnd, Part1.GND
  N3: LED1.anode, R3.Pin_0
  N4: LED2.anode, R2.Pin_0
  VDD: S1.Pin_1, S1.Pin_2, AM1.VDD, R5.Pin_1, R6.Pin_1, J2.Vcc, Part1.VIN
  N5: S1.Pin_3, S1.Pin_4

notes:
  KYTO2800D

custom parts:
  ESP32-38PinWide: Generic 38-Pin ESP32 with wide format (only access to one side of pins on a breadboard) based on Stephen Lilley's HiLetgo ESP-WROOM-32 ESP32 ESP-32S Development Board.
  AM2320 Humidity and Temperature Sensor: AM2320 I2C Humidity and Temperature Sensor
  Adafruit TSL2561: The TSL2561 luminosity sensor is an advanced digital light sensor, ideal for use in a wide range of light situations. Compared to low cost CdS cells, this sensor is more precise, allowing for exact lux calculations and can be configured for different gain/timing ranges to detect light ranges from up to 0.1 - 40,000+ Lux on the fly. The best part of this sensor is that it contains both infrared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
